// Logisim project CPU7.circ as structural Verilog: 7 circuits, main circuit main
// R1
module main (
);

  wire clk, F_sel, JAL_R, R_I, SW, undriven_2, Wdest, Wen, ZF;
  wire [1:0] func, multiplexer_5_out, PC_Control_out_3, Rw_RB;
  wire [2:0] multiplexer_2_out;
  wire [4:0] op;
  wire [5:0] rom_3_data;
  wire [10:0] undriven;
  wire [10:2] rom_1_data;
  wire [18:0] adder_1_out, adder_2_out, adder_3_out, bit_extender_2_out, jalr, multiplexer_1_out;
  wire [19:0] PC_output;
  wire [19:2] alu_1_output_2;
  wire [31:0] alu_1_output, bit_extender_4_out, bit_extender_5_out, imm5, multiplexer_3_out,
       multiplexer_4_out, multiplexer_6_out, pc_1, ram_1_data, register_file_1_busb, register_file_1_r1,
       register_file_1_r2, register_file_1_r3, register_file_1_r4, register_file_1_r5, register_file_1_r6,
       register_file_1_r7, W;
  wire [31:19] adder_3_out_2, register_file_1_busa;

  Clock clock_1 (.out(clk));
  assign pc_1 = {{13{adder_1_out[18]}}, adder_1_out};  // Bit_Extender bit_extender_1
  PC PC (.\input (multiplexer_1_out), .clk(clk), .\output (PC_output));
  Multiplexer #(.select(2), .width(19), .enable("false")) multiplexer_1 (
    .in0(adder_1_out), .in1(adder_2_out), .in2(adder_3_out), .in3(jalr), .out(multiplexer_1_out),
    .sel(PC_Control_out_3));
  Adder #(.width(19)) adder_1 (.a(19'h1), .b(PC_output[19:1]), .out(adder_1_out));  // open: cin, cout
  PC_Control PC_Control (.op(op), .zero_flag(ZF), .out_3(PC_Control_out_3));
  ROM #(.addrWidth(20), .dataWidth(16)) rom_1 (.addr(PC_output), .data({op, rom_1_data, func}));  // open: sel
  ROM #(.addrWidth(5)) rom_2 (.addr(op), .data({JAL_R, F_sel, SW, Rw_RB, Wen, R_I, Wdest}));  // open: sel
  assign bit_extender_2_out = {{8{rom_1_data[10]}}, {rom_1_data, func}};  // Bit_Extender bit_extender_2
  Multiplexer #(.select(2), .width(3), .enable("false")) multiplexer_2 (
    .in0(rom_1_data[7:5]), .in1(rom_1_data[4:2]), .in2(3'b111), .out(multiplexer_2_out), .sel(Rw_RB));  // open: in3
  Adder #(.width(19)) adder_2 (.a(PC_output[19:1]), .b(bit_extender_2_out), .out(adder_2_out));  // open: cin, cout
  Register_File register_file_1 (
    .WriteEN(Wen), .RA(rom_1_data[10:8]), .RB(rom_1_data[7:5]), .W(multiplexer_3_out),
    .RW(multiplexer_2_out), .BusA({register_file_1_busa, jalr}), .BusB(register_file_1_busb), .clk(clk),
    .R1(register_file_1_r1), .R2(register_file_1_r2), .R3(register_file_1_r3), .R4(register_file_1_r4),
    .R5(register_file_1_r5), .R6(register_file_1_r6), .R7(register_file_1_r7));
  Multiplexer #(.width(32), .enable("false")) multiplexer_3 (.in0(W), .in1(pc_1), .out(multiplexer_3_out), .sel(JAL_R));
  assign imm5 = {{27{rom_1_data[4]}}, {rom_1_data[4:2], func}};  // Bit_Extender bit_extender_3
  assign bit_extender_4_out = {{16{undriven[10]}}, {undriven, rom_1_data[4:2], func}};  // Bit_Extender bit_extender_4
  assign bit_extender_5_out = {{13{PC_output[19]}}, PC_output[19:1]};  // Bit_Extender bit_extender_5
  // Probe on undriven_2
  Multiplexer #(.width(32), .enable("false")) multiplexer_4 (
    .in0(imm5), .in1(bit_extender_4_out), .out(multiplexer_4_out), .sel(1'b0));
  Adder #(.width(32)) adder_3 (
    .a(bit_extender_5_out), .b(imm5), .out({adder_3_out_2, adder_3_out}));  // open: cin, cout
  Multiplexer #(.width(2), .enable("false")) multiplexer_5 (
    .in0(2'b00), .in1(func), .out(multiplexer_5_out), .sel(F_sel));
  Multiplexer #(.width(32), .enable("false")) multiplexer_6 (
    .in0(register_file_1_busb), .in1(multiplexer_4_out), .out(multiplexer_6_out), .sel(R_I));
  ALU alu_1 (
    .Data_A({register_file_1_busa, jalr}), .Data_B(multiplexer_6_out),
    .\output ({alu_1_output[31:20], alu_1_output_2, alu_1_output[1:0]}), .ALUop(rom_3_data), .zero_flag(ZF));
  ROM #(.addrWidth(7), .dataWidth(6)) rom_3 (.addr({op, multiplexer_5_out}), .data(rom_3_data));  // open: sel
  RAM #(.addrWidth(20), .dataWidth(32), .bus("separate")) ram_1 (
    .addr({alu_1_output_2, 2'b00}), .din(register_file_1_busb), .data(ram_1_data), .str(SW), .clk(clk),
    .ld(Wdest));  // open: sel, clr
  Multiplexer #(.width(32), .enable("false")) multiplexer_7 (
    .in0({alu_1_output[31:20], alu_1_output_2, alu_1_output[1:0]}), .in1(ram_1_data), .out(W), .sel(Wdest));

  // Notes on the sheet:
  //   Main Control
  //   contents of rom_1 (hex, n*v repeats v):
  //   4024 0 aa21 0 a5c0 0 1dc 0 6681 0 86e1 0 e800 0 e800 7*0 aa80
  //   contents of rom_2 (hex, n*v repeats v):
  //   4c 4c 0 0 16*6 7 22 5*0 86 2 96
  //   Branch
  //   ALU Control
  //   contents of rom_3 (hex, n*v repeats v):
  //   0 4 8 c 1 21 2 12 12*0 4 0 0 0 8 0 0 0 c 0 0 0 1 0 0 0 21 0 0 0 2 0 0 0 12 0 0 0 3 0 0 0 7 0 0 0 b 0
  //   0 0 f 0 0 0 2 0 0 0 2 0 0 0 12 0 0 0 12 0 0 0 1 0 0 0 1
endmodule

module Shifter (
  input  [1:0] select,
  input  [31:0] _32_data,
  input  [4:0] _5_bit_shift_amount,
  output [31:0] \output 
);

  wire [31:0] shifter_1_out, shifter_2_out, shifter_3_out, shifter_4_out;

  Shifter_part #(.width(32)) shifter_1 (.in(_32_data), .\dist (_5_bit_shift_amount), .out(shifter_1_out));
  Shifter_part #(.width(32), .shift("lr")) shifter_2 (.in(_32_data), .\dist (_5_bit_shift_amount), .out(shifter_2_out));
  Shifter_part #(.width(32), .shift("ar")) shifter_3 (.in(_32_data), .\dist (_5_bit_shift_amount), .out(shifter_3_out));
  Shifter_part #(.width(32), .shift("rr")) shifter_4 (.in(_32_data), .\dist (_5_bit_shift_amount), .out(shifter_4_out));
  Multiplexer #(.select(2), .width(32)) multiplexer_1 (
    .in0(shifter_1_out), .in1(shifter_2_out), .in2(shifter_3_out), .in3(shifter_4_out), .out(\output ),
    .sel(select));  // open: en
endmodule

module ALU (
  input  [5:0] ALUop,
  input  [31:0] Data_A,
  input  [31:0] Data_B,
  output zero_flag,
  output [31:0] \output 
);

  wire comparator_1_eq, comparator_1_lt, multiplexer_2_out;
  wire [4:0] bit_extender_1_out;
  wire [31:0] adder_1_out, and_1_out, and_2_out, bit_extender_2_out, bit_extender_3_out, multiplexer_1_out,
       or_1_out, shifter_1_output, xor_1_out, xor_2_out;

  assign and_1_out = Data_A & Data_B;  // AND_Gate and_1, 32 bits wide
  assign and_2_out = ~Data_A & Data_B;  // AND_Gate and_2, 32 bits wide
  assign or_1_out = Data_A | Data_B;  // OR_Gate or_1, 32 bits wide
  assign xor_1_out = Data_A ^ Data_B;  // XOR_Gate xor_1, 32 bits wide
  Shifter shifter_1 (
    ._32_data(Data_B), ._5_bit_shift_amount(bit_extender_1_out), .\output (shifter_1_output),
    .select(ALUop[3:2]));
  Bit_Extender #(.in_width(32), .out_width(5)) bit_extender_1 (.in(Data_A), .out(bit_extender_1_out));
  assign bit_extender_2_out = {{31{ALUop[5]}}, ALUop[5]};  // Bit_Extender bit_extender_2
  Multiplexer #(.select(2), .width(32), .enable("false")) multiplexer_1 (
    .in0(and_1_out), .in1(and_2_out), .in2(or_1_out), .in3(xor_1_out), .out(multiplexer_1_out),
    .sel(ALUop[3:2]));
  assign xor_2_out = bit_extender_2_out ^ Data_A;  // XOR_Gate xor_2, 32 bits wide
  Adder #(.width(32)) adder_1 (.a(xor_2_out), .b(Data_B), .out(adder_1_out), .cin(ALUop[5]));  // open: cout
  Comparator #(.width(32)) comparator_1 (
    .a(Data_A), .b(Data_B), .eq(comparator_1_eq), .lt(comparator_1_lt));  // open: gt
  assign bit_extender_3_out = {{31{1'b0}}, multiplexer_2_out};  // Bit_Extender bit_extender_3
  Multiplexer #(.enable("false")) multiplexer_2 (
    .in0(comparator_1_eq), .in1(comparator_1_lt), .out(multiplexer_2_out), .sel(ALUop[4]));
  Multiplexer #(.select(2), .width(32), .enable("false")) multiplexer_3 (
    .in0(multiplexer_1_out), .in1(adder_1_out), .in2(bit_extender_3_out), .in3(shifter_1_output),
    .out(\output ), .sel(ALUop[1:0]));
  not not_1 (zero_flag, \output [0]);

  // Other names for the same wires on the sheet: ALUsel[1:0] = ALUop[1:0]; sel[1:0] = ALUop[3:2]; comp = ALUop[4];
  //   sign = ALUop[5]
endmodule

module PC (
  input  [18:0] \input ,
  input  clk,
  output [19:0] \output 
);

  Register #(.width(19)) register_1 (.D(\input ), .en(1'b1), .Q(\output [19:1]), .clk(clk));  // open: clr

  assign \output [0] = 1'b0;
endmodule

// Registers
module Register_File (
  input  [2:0] RA,
  input  [2:0] RB,
  input  [2:0] RW,
  input  [31:0] W,
  input  WriteEN,
  input  clk,
  output [31:0] R1,
  output [31:0] R2,
  output [31:0] BusA,
  output [31:0] R3,
  output [31:0] BusB,
  output [31:0] R4,
  output [31:0] R5,
  output [31:0] R6,
  output [31:0] R7
);

  wire and_1_out, and_2_out, and_3_out, and_4_out, and_5_out, and_6_out, and_7_out, decoder_1_out1,
       decoder_1_out2, decoder_1_out3, decoder_1_out4, decoder_1_out5, decoder_1_out6, decoder_1_out7,
       decoder_2_out0, decoder_2_out1, decoder_2_out2, decoder_2_out3, decoder_2_out4, decoder_2_out5,
       decoder_2_out6, decoder_2_out7, decoder_3_out0, decoder_3_out1, decoder_3_out2, decoder_3_out3,
       decoder_3_out4, decoder_3_out5, decoder_3_out6, decoder_3_out7;

  Decoder #(.select(3), .enable("false")) decoder_1 (
    .out1(decoder_1_out1), .out2(decoder_1_out2), .out3(decoder_1_out3), .out4(decoder_1_out4),
    .out5(decoder_1_out5), .out6(decoder_1_out6), .out7(decoder_1_out7), .sel(RW));  // open: out0
  and and_1 (and_1_out, decoder_1_out1, WriteEN);
  and and_2 (and_2_out, decoder_1_out2, WriteEN);
  and and_3 (and_3_out, decoder_1_out3, WriteEN);
  and and_4 (and_4_out, decoder_1_out4, WriteEN);
  and and_5 (and_5_out, decoder_1_out5, WriteEN);
  and and_6 (and_6_out, decoder_1_out6, WriteEN);
  and and_7 (and_7_out, decoder_1_out7, WriteEN);
  Register #(.width(32), .trigger("low")) u_R1 (.D(W), .en(and_1_out), .Q(R1), .clk(clk));  // open: clr
  Register #(.width(32), .trigger("low")) u_R2 (.D(W), .en(and_2_out), .Q(R2), .clk(clk));  // open: clr
  Register #(.width(32), .trigger("low")) u_R3 (.D(W), .en(and_3_out), .Q(R3), .clk(clk));  // open: clr
  Register #(.width(32), .trigger("low")) u_R4 (.D(W), .en(and_4_out), .Q(R4), .clk(clk));  // open: clr
  Register #(.width(32), .trigger("low")) u_R5 (.D(W), .en(and_5_out), .Q(R5), .clk(clk));  // open: clr
  Register #(.width(32), .trigger("low")) u_R6 (.D(W), .en(and_6_out), .Q(R6), .clk(clk));  // open: clr
  Register #(.width(32), .trigger("low")) u_R7 (.D(W), .en(and_7_out), .Q(R7), .clk(clk));  // open: clr
  assign BusA = decoder_2_out0 ? {32{1'b0}} : 32'bz;  // Controlled_Buffer controlled_buffer_1
  assign BusA = decoder_2_out1 ? R1 : 32'bz;  // Controlled_Buffer controlled_buffer_2
  assign BusA = decoder_2_out2 ? R2 : 32'bz;  // Controlled_Buffer controlled_buffer_3
  assign BusA = decoder_2_out3 ? R3 : 32'bz;  // Controlled_Buffer controlled_buffer_4
  assign BusA = decoder_2_out4 ? R4 : 32'bz;  // Controlled_Buffer controlled_buffer_5
  assign BusA = decoder_2_out5 ? R5 : 32'bz;  // Controlled_Buffer controlled_buffer_6
  assign BusA = decoder_2_out6 ? R6 : 32'bz;  // Controlled_Buffer controlled_buffer_7
  assign BusA = decoder_2_out7 ? R7 : 32'bz;  // Controlled_Buffer controlled_buffer_8
  Decoder #(.select(3), .enable("false")) decoder_2 (
    .out0(decoder_2_out0), .out1(decoder_2_out1), .out2(decoder_2_out2), .out3(decoder_2_out3),
    .out4(decoder_2_out4), .out5(decoder_2_out5), .out6(decoder_2_out6), .out7(decoder_2_out7), .sel(RA));
  assign BusB = decoder_3_out0 ? {32{1'b0}} : 32'bz;  // Controlled_Buffer controlled_buffer_9
  assign BusB = decoder_3_out1 ? R1 : 32'bz;  // Controlled_Buffer controlled_buffer_10
  assign BusB = decoder_3_out2 ? R2 : 32'bz;  // Controlled_Buffer controlled_buffer_11
  assign BusB = decoder_3_out3 ? R3 : 32'bz;  // Controlled_Buffer controlled_buffer_12
  assign BusB = decoder_3_out4 ? R4 : 32'bz;  // Controlled_Buffer controlled_buffer_13
  assign BusB = decoder_3_out5 ? R5 : 32'bz;  // Controlled_Buffer controlled_buffer_14
  assign BusB = decoder_3_out6 ? R6 : 32'bz;  // Controlled_Buffer controlled_buffer_15
  assign BusB = decoder_3_out7 ? R7 : 32'bz;  // Controlled_Buffer controlled_buffer_16
  Decoder #(.select(3), .enable("false")) decoder_3 (
    .out0(decoder_3_out0), .out1(decoder_3_out1), .out2(decoder_3_out2), .out3(decoder_3_out3),
    .out4(decoder_3_out4), .out5(decoder_3_out5), .out6(decoder_3_out6), .out7(decoder_3_out7), .sel(RB));

  // Other names for the same wires on the sheet: RA_t[31:0] = BusA; RB_t[31:0] = BusB
endmodule

// Instruction mem
module instruction_memory (
  input  [19:0] in_1,
  output imm_signal,
  output [15:0] imm,
  output [15:0] inst
);

  wire and_1_out, clock_1_out, not_1_out, not_2_out;
  wire [2:0] counter_1_q;
  wire [7:0] imm11_0_7_out, imm11_8_15_out, ram_1_data;
  wire [19:0] counter_2_q;

  not not_1 (not_1_out, counter_1_q[2]);
  Counter #(.width(3), .max('h7), .ongoal("stay")) counter_1 (
    .count(not_2_out), .Q(counter_1_q), .clk(clock_1_out), .clr(and_1_out));  // open: load, D, carry
  not not_2 (not_2_out, and_1_out);
  and and_1 (and_1_out, counter_1_q[2], counter_1_q[0]);
  Counter #(.width(20), .max('hfffff), .ongoal("stay")) counter_2 (
    .load(counter_1_q[2]), .D(in_1), .count(not_1_out), .Q(counter_2_q), .clk(clock_1_out));  // open: carry, clr
  Clock clock_1 (.out(clock_1_out));
  RAM #(.addrWidth(20)) ram_1 (.addr(counter_2_q), .data(ram_1_data), .clk(clock_1_out), .ld(1'b1));  // open: sel, clr
  Shift_Register #(.width(8), .length(1)) imm11_0_7 (
    .in(ram_1_data), .clk(clock_1_out), .out(imm11_0_7_out));  // open: shift, load, clr, d0, q0
  and and_2 (imm_signal, imm11_8_15_out[7], imm11_8_15_out[6], imm11_8_15_out[5], imm11_8_15_out[4], ~imm11_8_15_out[3]);  // AND_Gate
  Shift_Register #(.width(8), .length(1)) imm11_8_15 (
    .in(imm11_0_7_out), .clk(clock_1_out), .out(imm11_8_15_out));  // open: shift, load, clr, d0, q0
  Shift_Register #(.width(8), .length(1)) _0_7 (
    .in(imm11_8_15_out), .clk(clock_1_out), .out(inst[7:0]));  // open: shift, load, clr, d0, q0
  Shift_Register #(.width(8), .length(1)) _8_15 (
    .in(inst[7:0]), .clk(clock_1_out), .out(inst[15:8]));  // open: shift, load, clr, d0, q0
  assign imm = imm_signal ? {imm11_8_15_out, imm11_0_7_out} : 16'bz;  // Controlled_Buffer controlled_buffer_1
endmodule

module PC_Control (
  input  [4:0] op,
  input  zero_flag,
  output [1:0] out_3
);

  wire and_1_out, and_2_out, and_3_out, and_4_out, decoder_1_out16, decoder_1_out17, decoder_1_out18,
       decoder_1_out19, decoder_1_out27, decoder_1_out28, decoder_1_out29, nor_1_out, or_1_out;

  Decoder #(.select(5), .enable("false")) decoder_1 (
    .out16(decoder_1_out16), .out17(decoder_1_out17), .out18(decoder_1_out18), .out19(decoder_1_out19),
    .out27(decoder_1_out27), .out28(decoder_1_out28), .out29(decoder_1_out29), .sel(op));  // open: out0, out1, out2, out3, out4, out5, out6, out7, out8, out9, out10, out11, out12, out13, out14, out15, out20, out21, out22, out23, out24, out25, out26, out30, out31
  and and_1 (and_1_out, decoder_1_out17, ~zero_flag);  // AND_Gate
  and and_2 (and_2_out, decoder_1_out16, zero_flag);
  or or_1 (or_1_out, and_2_out, and_1_out, and_4_out, and_3_out);
  assign out_3 = or_1_out ? 2'b10 : 2'bz;  // Controlled_Buffer controlled_buffer_1
  and and_3 (and_3_out, decoder_1_out19, ~zero_flag);  // AND_Gate
  and and_4 (and_4_out, decoder_1_out18, zero_flag);
  assign out_3 = decoder_1_out27 ? 2'b11 : 2'bz;  // Controlled_Buffer controlled_buffer_2
  assign out_3 = decoder_1_out28 ? 2'b01 : 2'bz;  // Controlled_Buffer controlled_buffer_3
  assign out_3 = decoder_1_out29 ? 2'b01 : 2'bz;  // Controlled_Buffer controlled_buffer_4
  assign out_3 = nor_1_out ? 2'b00 : 2'bz;  // Controlled_Buffer controlled_buffer_5
  nor nor_1 (nor_1_out, or_1_out, decoder_1_out27, decoder_1_out28, decoder_1_out29);
endmodule
